# Fritzing sketch estacionMeteorologica (saved by Fritzing 0.9.4)
breadboards: 1

parts:
  Part1 = Arduino Nano (Rev3.0) (ICSP)
  DHT1 = DHT22 Humidity and Temperature Sensor
  Part2 = Barometric Pressure Sensor - BMP180 Breakout (GY-68)
  LCD2 = TFT 1.8 inch 160x128 w SD
  BATT1 = 4xAA Switchable Battery Pack w/Bare Wire
  J2 = Power Jack [package=power_jack_smd]
  JACK1 = 2.1mm Barrel Jack with Terminal Block

nets:
  GND: Part1.GND, DHT1.GND, Part2.GND, LCD2.pin2, J2.GND
  N1: Part1.D7, DHT1.DATA
  N2: Part1.D8, LCD2.pin_5
  N3: Part1.D9, LCD2.pin4
  N4: Part1.D10, LCD2.pin3
  N5: Part1.D11/MOSI, LCD2.pin_6
  5V: Part1.5V, DHT1.VDD, Part2.VCC, LCD2.pin_1, J2.GNDBREAK
  N6: Part1.A5, Part2.SCL
  N7: Part1.A4, Part2.SDA
  N8: Part1.3V3, LCD2.pin_8
  N9: Part1.D13/SCK, LCD2.pin_7
  N10: BATT1.POS, JACK1.POS
  N11: BATT1.NEG, JACK1.NEG

custom parts:
  TFT 1.8 inch 160x128 w SD: This is a generic 1.8 tft spi lcd display available on ebay and others. The 1.8" display has 128x160 color pixels.
  4xAA Switchable Battery Pack w/Bare Wire: 4xAA Switchable Battery Pack with Bare Wire connection
